// Logisim project LIFO.circ as structural Verilog: 1 circuit, main circuit main
module main (
  input  [7:0] in_1,
  input  POP,
  input  EN,
  input  in_4,
  output [7:0] out_5
);

  wire and_1_out, and_2_out, clock_1_out, not_1_out, not_2_out;
  wire [2:0] multiplexer_1_out, Peak_1_q, Peak_q;

  not not_1 (not_1_out, POP);
  and and_1 (and_1_out, POP, EN);
  and and_2 (and_2_out, not_1_out, EN);
  Clock clock_1 (.out(clock_1_out));
  Counter #(.width(3), .max('h7)) Peak (
    .load(and_1_out), .count(EN), .Q(Peak_q), .clk(clock_1_out));  // open: D, carry, clr
  Counter #(.width(3), .max('h7)) Peak_1 (
    .load(and_1_out), .count(EN), .Q(Peak_1_q), .clk(clock_1_out));  // open: D, carry, clr
  Multiplexer #(.width(3), .enable("false")) multiplexer_1 (
    .in0(Peak_q), .in1(Peak_1_q), .out(multiplexer_1_out), .sel(and_1_out));
  not not_2 (not_2_out, and_2_out);
  RAM #(.addrWidth(3), .bus("separate")) ram_1 (
    .addr(multiplexer_1_out), .din(in_1), .data(out_5), .str(and_2_out), .sel(EN), .clk(clock_1_out),
    .ld(not_2_out), .clr(in_4));
endmodule
