// Logisim project LIFOusingUSR.circ as structural Verilog: 1 circuit, main circuit main
module main (
  input  I3,
  input  I2,
  input  I1,
  input  POP,
  input  EN,
  input  I0,
  output O3,
  output O2,
  output O1,
  output O0,
  output [1:0] out_11
);

  wire clock_1_out;
  wire [0:0] and_1_out;

  and and_1 (and_1_out[0], POP, EN);
  Clock clock_1 (.out(clock_1_out));
  Counter #(.width(2), .max('h3)) counter_1 (
    .load(and_1_out[0]), .count(EN), .Q(out_11), .clk(clock_1_out));  // open: D, carry, clr
  universalshiftregister_main main_1 (
    .in_5({EN, and_1_out[0]}), .IL(I3), .Ir(1'b0), .O3(O3), .in_8(clock_1_out));  // open: I3, I2, I1, I0, O2, O1, O0
  universalshiftregister_main main_2 (
    .in_5({EN, and_1_out[0]}), .IL(I2), .Ir(1'b0), .O3(O2), .in_8(clock_1_out));  // open: I3, I2, I1, I0, O2, O1, O0
  universalshiftregister_main main_3 (
    .in_5({EN, and_1_out[0]}), .IL(I1), .Ir(1'b0), .O3(O1), .in_8(clock_1_out));  // open: I3, I2, I1, I0, O2, O1, O0
  universalshiftregister_main main_4 (
    .in_5({EN, and_1_out[0]}), .IL(I0), .Ir(1'b0), .O3(O0), .in_8(clock_1_out));  // open: I3, I2, I1, I0, O2, O1, O0
endmodule
