// Logisim project universalshiftregister.circ as structural Verilog: 1 circuit, main circuit main
module main (
  input  I3,
  input  I2,
  input  I1,
  input  I0,
  input  [1:0] in_5,
  input  IL,
  input  Ir,
  input  in_8,
  output O3,
  output O2,
  output O1,
  output O0
);

  wire multiplexer_1_out, multiplexer_2_out, multiplexer_3_out, multiplexer_4_out;

  Multiplexer #(.select(2), .enable("false")) multiplexer_1 (
    .in0(O3), .in1(I3), .in2(IL), .in3(O2), .out(multiplexer_1_out), .sel(in_5));
  D_Flip_Flop d_ff_1 (.clk(in_8), .D(multiplexer_1_out), .Q(O3));  // open: Qn, preset, en, reset
  Multiplexer #(.select(2), .enable("false")) multiplexer_2 (
    .in0(O2), .in1(I2), .in2(O3), .in3(O1), .out(multiplexer_2_out), .sel(in_5));
  D_Flip_Flop d_ff_2 (.clk(in_8), .D(multiplexer_2_out), .Q(O2));  // open: Qn, preset, en, reset
  Multiplexer #(.select(2), .enable("false")) multiplexer_3 (
    .in0(O1), .in1(I1), .in2(O2), .in3(O0), .out(multiplexer_3_out), .sel(in_5));
  D_Flip_Flop d_ff_3 (.clk(in_8), .D(multiplexer_3_out), .Q(O1));  // open: Qn, preset, en, reset
  Multiplexer #(.select(2), .enable("false")) multiplexer_4 (
    .in0(O0), .in1(I0), .in2(O1), .in3(Ir), .out(multiplexer_4_out), .sel(in_5));
  D_Flip_Flop d_ff_4 (.clk(in_8), .D(multiplexer_4_out), .Q(O0));  // open: Qn, preset, en, reset
endmodule
